// Logisim project ALU.circ as structural Verilog
module main (
  input  [2:0] ALU_OP,
  input  [31:0] SRC1,
  input  [31:0] SRC2,
  input  SUB,
  output [31:0] ALU_RESULT
);

  wire comparator_1_eq;
  wire [31:0] adder_1_out, adder_2_out, AND_out, bit_extender_1_out, not_1_out, OR_out;

  assign not_1_out = ~SRC2;  // NOT_Gate not_1, 32 bits wide
  assign AND_out = SRC1 & SRC2;  // AND_Gate AND, 32 bits wide
  assign OR_out = SRC1 | SRC2;  // OR_Gate OR, 32 bits wide
  Adder #(.width(32)) adder_1 (.a(SRC1), .b(SRC2), .out(adder_1_out));  // open: cin, cout
  Adder #(.width(32)) adder_2 (.a(SRC1), .b(not_1_out), .out(adder_2_out), .cin(SUB));  // open: cout
  assign bit_extender_1_out = {{31{1'b0}}, adder_2_out[31]};  // Bit_Extender bit_extender_1
  Multiplexer #(.select(3), .width(32), .enable("false")) multiplexer_1 (
    .in0(AND_out), .in1(OR_out), .in2(adder_1_out), .in6(adder_2_out), .in7(bit_extender_1_out),
    .out(ALU_RESULT), .sel(ALU_OP));  // open: in3, in4, in5
  LED ZERO (.in(comparator_1_eq));
  Comparator #(.width(32)) comparator_1 (.a({32{1'b0}}), .b(ALU_RESULT), .eq(comparator_1_eq));  // open: gt, lt
endmodule
