// Logisim project Read_Write_Port.circ as structural Verilog: 2 circuits, main circuit main
// Read_Write_Port
module main (
  input  Write_Data,
  input  Clock,
  input  [4:0] Read_Reg_1,
  input  [4:0] Write_Reg,
  input  [4:0] Read_Reg_2,
  input  [31:0] Write_Data_2,
  output [31:0] Read_Data_1,
  output [31:0] Read_Data_2
);

  wire and_1_out, and_2_out, and_3_out, and_4_out, and_5_out, and_6_out, and_7_out, and_8_out, and_9_out,
       and_10_out, and_11_out, and_12_out, and_13_out, and_14_out, and_15_out, and_16_out, and_17_out,
       and_18_out, and_19_out, and_20_out, and_21_out, and_22_out, and_23_out, and_24_out, and_25_out,
       and_26_out, and_27_out, and_28_out, and_29_out, and_30_out, and_31_out, and_32_out, decoder_1_out0,
       decoder_1_out1, decoder_1_out2, decoder_1_out3, decoder_1_out4, decoder_1_out5, decoder_1_out6,
       decoder_1_out7, decoder_1_out8, decoder_1_out9, decoder_1_out10, decoder_1_out11, decoder_1_out12,
       decoder_1_out13, decoder_1_out14, decoder_1_out15, decoder_1_out16, decoder_1_out17, decoder_1_out18,
       decoder_1_out19, decoder_1_out20, decoder_1_out21, decoder_1_out22, decoder_1_out23, decoder_1_out24,
       decoder_1_out25, decoder_1_out26, decoder_1_out27, decoder_1_out28, decoder_1_out29, decoder_1_out30,
       decoder_1_out31;
  wire [31:0] r0_q, r1_q, r2_q, r3_q, r4_q, r5_q, r6_q, r7_q, r8_q, r9_q, r10_q, r11_q, r12_q, r13_q, r14_q,
       r15_q, r16_q, r17_q, r18_q, r19_q, r20_q, r21_q, r22_q, r23_q, r24_q, r25_q, r26_q, r27_q, r28_q,
       r29_q, r30_q, r31_q;

  Decoder #(.select(5), .enable("false")) decoder_1 (
    .out0(decoder_1_out0), .out1(decoder_1_out1), .out2(decoder_1_out2), .out3(decoder_1_out3),
    .out4(decoder_1_out4), .out5(decoder_1_out5), .out6(decoder_1_out6), .out7(decoder_1_out7),
    .out8(decoder_1_out8), .out9(decoder_1_out9), .out10(decoder_1_out10), .out11(decoder_1_out11),
    .out12(decoder_1_out12), .out13(decoder_1_out13), .out14(decoder_1_out14), .out15(decoder_1_out15),
    .out16(decoder_1_out16), .out17(decoder_1_out17), .out18(decoder_1_out18), .out19(decoder_1_out19),
    .out20(decoder_1_out20), .out21(decoder_1_out21), .out22(decoder_1_out22), .out23(decoder_1_out23),
    .out24(decoder_1_out24), .out25(decoder_1_out25), .out26(decoder_1_out26), .out27(decoder_1_out27),
    .out28(decoder_1_out28), .out29(decoder_1_out29), .out30(decoder_1_out30), .out31(decoder_1_out31),
    .sel(Write_Reg));
  and and_1 (and_1_out, decoder_1_out0, Write_Data);
  and and_2 (and_2_out, decoder_1_out1, Write_Data);
  and and_3 (and_3_out, decoder_1_out2, Write_Data);
  and and_4 (and_4_out, decoder_1_out3, Write_Data);
  and and_5 (and_5_out, decoder_1_out4, Write_Data);
  and and_6 (and_6_out, decoder_1_out5, Write_Data);
  and and_7 (and_7_out, decoder_1_out6, Write_Data);
  and and_8 (and_8_out, decoder_1_out7, Write_Data);
  and and_9 (and_9_out, decoder_1_out8, Write_Data);
  and and_10 (and_10_out, decoder_1_out9, Write_Data);
  and and_11 (and_11_out, decoder_1_out10, Write_Data);
  and and_12 (and_12_out, decoder_1_out11, Write_Data);
  and and_13 (and_13_out, decoder_1_out12, Write_Data);
  and and_14 (and_14_out, decoder_1_out13, Write_Data);
  and and_15 (and_15_out, decoder_1_out14, Write_Data);
  and and_16 (and_16_out, decoder_1_out15, Write_Data);
  and and_17 (and_17_out, decoder_1_out16, Write_Data);
  and and_18 (and_18_out, decoder_1_out17, Write_Data);
  and and_19 (and_19_out, decoder_1_out18, Write_Data);
  and and_20 (and_20_out, decoder_1_out19, Write_Data);
  and and_21 (and_21_out, decoder_1_out20, Write_Data);
  and and_22 (and_22_out, decoder_1_out21, Write_Data);
  and and_23 (and_23_out, decoder_1_out22, Write_Data);
  and and_24 (and_24_out, decoder_1_out23, Write_Data);
  and and_25 (and_25_out, decoder_1_out24, Write_Data);
  and and_26 (and_26_out, decoder_1_out25, Write_Data);
  and and_27 (and_27_out, decoder_1_out26, Write_Data);
  and and_28 (and_28_out, decoder_1_out27, Write_Data);
  and and_29 (and_29_out, decoder_1_out28, Write_Data);
  and and_30 (and_30_out, decoder_1_out29, Write_Data);
  and and_31 (and_31_out, decoder_1_out30, Write_Data);
  and and_32 (and_32_out, decoder_1_out31, Write_Data);
  Register #(.width(32)) r0 (.D(Write_Data_2), .en(and_1_out), .Q(r0_q), .clk(Clock));  // open: clr
  Register #(.width(32)) r1 (.D(Write_Data_2), .en(and_2_out), .Q(r1_q), .clk(Clock));  // open: clr
  Register #(.width(32)) r2 (.D(Write_Data_2), .en(and_3_out), .Q(r2_q), .clk(Clock));  // open: clr
  Register #(.width(32)) r3 (.D(Write_Data_2), .en(and_4_out), .Q(r3_q), .clk(Clock));  // open: clr
  Register #(.width(32)) r4 (.D(Write_Data_2), .en(and_5_out), .Q(r4_q), .clk(Clock));  // open: clr
  Register #(.width(32)) r5 (.D(Write_Data_2), .en(and_6_out), .Q(r5_q), .clk(Clock));  // open: clr
  Register #(.width(32)) r6 (.D(Write_Data_2), .en(and_7_out), .Q(r6_q), .clk(Clock));  // open: clr
  Register #(.width(32)) r7 (.D(Write_Data_2), .en(and_8_out), .Q(r7_q), .clk(Clock));  // open: clr
  Register #(.width(32)) r8 (.D(Write_Data_2), .en(and_9_out), .Q(r8_q), .clk(Clock));  // open: clr
  Register #(.width(32)) r9 (.D(Write_Data_2), .en(and_10_out), .Q(r9_q), .clk(Clock));  // open: clr
  Register #(.width(32)) r10 (.D(Write_Data_2), .en(and_11_out), .Q(r10_q), .clk(Clock));  // open: clr
  Register #(.width(32)) r11 (.D(Write_Data_2), .en(and_12_out), .Q(r11_q), .clk(Clock));  // open: clr
  Register #(.width(32)) r12 (.D(Write_Data_2), .en(and_13_out), .Q(r12_q), .clk(Clock));  // open: clr
  Register #(.width(32)) r13 (.D(Write_Data_2), .en(and_14_out), .Q(r13_q), .clk(Clock));  // open: clr
  Register #(.width(32)) r14 (.D(Write_Data_2), .en(and_15_out), .Q(r14_q), .clk(Clock));  // open: clr
  Register #(.width(32)) r15 (.D(Write_Data_2), .en(and_16_out), .Q(r15_q), .clk(Clock));  // open: clr
  Register #(.width(32)) r16 (.D(Write_Data_2), .en(and_17_out), .Q(r16_q), .clk(Clock));  // open: clr
  Register #(.width(32)) r17 (.D(Write_Data_2), .en(and_18_out), .Q(r17_q), .clk(Clock));  // open: clr
  Register #(.width(32)) r18 (.D(Write_Data_2), .en(and_19_out), .Q(r18_q), .clk(Clock));  // open: clr
  Register #(.width(32)) r19 (.D(Write_Data_2), .en(and_20_out), .Q(r19_q), .clk(Clock));  // open: clr
  Register #(.width(32)) r20 (.D(Write_Data_2), .en(and_21_out), .Q(r20_q), .clk(Clock));  // open: clr
  Register #(.width(32)) r21 (.D(Write_Data_2), .en(and_22_out), .Q(r21_q), .clk(Clock));  // open: clr
  Register #(.width(32)) r22 (.D(Write_Data_2), .en(and_23_out), .Q(r22_q), .clk(Clock));  // open: clr
  Register #(.width(32)) r23 (.D(Write_Data_2), .en(and_24_out), .Q(r23_q), .clk(Clock));  // open: clr
  Register #(.width(32)) r24 (.D(Write_Data_2), .en(and_25_out), .Q(r24_q), .clk(Clock));  // open: clr
  Register #(.width(32)) r25 (.D(Write_Data_2), .en(and_26_out), .Q(r25_q), .clk(Clock));  // open: clr
  Register #(.width(32)) r26 (.D(Write_Data_2), .en(and_27_out), .Q(r26_q), .clk(Clock));  // open: clr
  Register #(.width(32)) r27 (.D(Write_Data_2), .en(and_28_out), .Q(r27_q), .clk(Clock));  // open: clr
  Register #(.width(32)) r28 (.D(Write_Data_2), .en(and_29_out), .Q(r28_q), .clk(Clock));  // open: clr
  Register #(.width(32)) r29 (.D(Write_Data_2), .en(and_30_out), .Q(r29_q), .clk(Clock));  // open: clr
  Register #(.width(32)) r30 (.D(Write_Data_2), .en(and_31_out), .Q(r30_q), .clk(Clock));  // open: clr
  Register #(.width(32)) r31 (.D(Write_Data_2), .en(and_32_out), .Q(r31_q), .clk(Clock));  // open: clr
  Multiplexer #(.select(5), .width(32), .enable("false")) multiplexer_1 (
    .in0(r0_q), .in1(r1_q), .in2(r2_q), .in3(r3_q), .in4(r4_q), .in5(r5_q), .in6(r6_q), .in7(r7_q),
    .in8(r8_q), .in9(r9_q), .in10(r10_q), .in11(r11_q), .in12(r12_q), .in13(r13_q), .in14(r14_q),
    .in15(r15_q), .in16(r16_q), .in17(r17_q), .in18(r18_q), .in19(r19_q), .in20(r20_q), .in21(r21_q),
    .in22(r22_q), .in23(r23_q), .in24(r24_q), .in25(r25_q), .in26(r26_q), .in27(r27_q), .in28(r28_q),
    .in29(r29_q), .in30(r30_q), .in31(r31_q), .out(Read_Data_1), .sel(Read_Reg_1));
  Multiplexer #(.select(5), .width(32), .enable("false")) multiplexer_2 (
    .in0(r0_q), .in1(r1_q), .in2(r2_q), .in3(r3_q), .in4(r4_q), .in5(r5_q), .in6(r6_q), .in7(r7_q),
    .in8(r8_q), .in9(r9_q), .in10(r10_q), .in11(r11_q), .in12(r12_q), .in13(r13_q), .in14(r14_q),
    .in15(r15_q), .in16(r16_q), .in17(r17_q), .in18(r18_q), .in19(r19_q), .in20(r20_q), .in21(r21_q),
    .in22(r22_q), .in23(r23_q), .in24(r24_q), .in25(r25_q), .in26(r26_q), .in27(r27_q), .in28(r28_q),
    .in29(r29_q), .in30(r30_q), .in31(r31_q), .out(Read_Data_2), .sel(Read_Reg_2));
endmodule

module Read_Write_Port (
  input  Write_reg,
  input  [4:0] Read_Reg_1,
  input  [4:0] Read_Reg_2,
  input  [4:0] Write_reg_2,
  input  [31:0] Write_Data,
  input  Clock,
  output [31:0] Read_Data_1,
  output [31:0] Read_Data_2
);

  main main_1 (
    .Write_Data(Write_reg), .Read_Reg_1(Read_Reg_1), .Write_Reg(Write_reg_2), .Read_Reg_2(Read_Reg_2),
    .Write_Data_2(Write_Data), .Clock(Clock), .Read_Data_1(Read_Data_1), .Read_Data_2(Read_Data_2));
endmodule
